# Fritzing sketch FlorArtist (saved by Fritzing 0.9.2b)
circuit board: 8.46667cm x 5.64444cm
breadboards: 1

parts:
  R1 = Resistor [tolerance=±5% resistance=220 package=THT]
  R2 = Resistor [tolerance=±5% resistance=220 package=THT]
  R3 = Photocell (LDR) [package=THT]
  R4 = Photocell (LDR) [package=THT]
  R5 = Slide Potentiometer [maximum_resistance=100kΩ]
  R6 = Slide Potentiometer [maximum_resistance=100kΩ]
  J1 = Infrared Proximity Sensor
  T1 = LM35 Temperature Sensor [package="TO92 [THT]"]
  Componente1 = Arduino Uno (Rev3)

nets:
  N1: R1.Pin_0, R4.pin_1, Componente1.A1
  GND: R1.Pin_1, R2.Pin_0, R5.leg2, R6.leg2, J1.GND, T1.GND
  N2: R2.Pin_1, R3.pin_0, Componente1.A0
  N3: R3.pin_1, R4.pin_0, R5.leg1, R6.leg1, J1.Vcc, T1.+Vs
  N4: R5.wiper, Componente1.A3
  N5: R6.wiper, Componente1.A2
  N6: J1.Vout, Componente1.A5/SCL
  N7: T1.Vout, Componente1.A4/SDA
